# Fritzing sketch helmet_rgb_breath_led_release (saved by Fritzing 0.9.3b)
breadboards: 1

parts:
  U1 = Battery Holders [package=battery-aa-kit]
  U3 = ATTINY45 [package=dip]
  R1 = Resistor [tolerance=±5% resistance=1.2k package="0402 [SMD]"]
  U4 = WS2812 RGB LED matrix 1x8
  U5 = WS2812 RGB LED matrix 1x8

nets:
  VCC: U1.+, U3.VCC, U4.VCC, U5.VCC
  GND: U1.-, U3.GND, U4.GND, U5.GND
  N1: U3.PB1(MISO), R1.Pin_0
  N2: R1.Pin_1, U4.DIN, U5.DIN

notes:
  14500 800mAh 3.7V
  ATTiny85
  W2812B 1x15
  安全帽呼吸燈 - 發行板
  羽山秋人 https://3wa.tw
  2024-07-07
  1.2KΩ

custom parts:
  WS2812 RGB LED matrix 1x8: WS2812 matrix 1x8
